# Fritzing sketch SchemaDesign (saved by Fritzing 0.7.1b)
breadboards: 1

parts:
  Arduino1 = Arduino
  TLC5940NT1 = IC, DIP package, 28 pins [chip_label=TLC5940NT spacing=300mil]
  VCC1 = Battery
  R1 = Resistor [tolerance=±5% resistance=390 package=THT]
  R2 = Resistor [tolerance=±5% resistance=10k package=THT]
  LED1 = RGB LED (com. anode, rbg) [package="5 mm [THT]"]

nets:
  N1: Arduino1.D13, TLC5940NT1.pin25
  N2: Arduino1.D11, TLC5940NT1.pin26
  N3: Arduino1.D10, TLC5940NT1.pin23, R2.Pin_0
  N4: Arduino1.D9, TLC5940NT1.pin24
  N5: Arduino1.D3, TLC5940NT1.pin18
  N6: Arduino1.+5V, TLC5940NT1.pin19, TLC5940NT1.pin21, R2.Pin_1
  N7: TLC5940NT1.pin2, LED1.blue_cathode
  N8: TLC5940NT1.pin3, LED1.green_cathode
  N9: TLC5940NT1.pin20, R1.Pin_1
  N10: TLC5940NT1.pin22, VCC1.-, R1.Pin_0
  N11: VCC1.+, LED1.red_cathode
